# Fritzing sketch Taller_RaspberryPi_HC-SR04 (saved by Fritzing 0.8.0b)
breadboards: 1

parts:
  Raspberry_Pi1 = Raspberry Pi
  Parte3 = SRF05 Ultrasonic Rangefinder
  R1 = Resistor [tolerance=±5% resistance=1k package="1206 [SMD]"]
  VCC1 = Battery  # not connected

nets:
  5V: Raspberry_Pi1.5V, Parte3.VCC
  N1: Raspberry_Pi1.I2C_SCL_0, Parte3.GND
  N2: Raspberry_Pi1.GPIO7, Raspberry_Pi1.GPIO3
  N3: Raspberry_Pi1.SPI_SCLK, Parte3.Echo, R1.Pin_0, R1.Pin_1
  N4: Raspberry_Pi1.SPI_CE1_N, Parte3.Trig
